# Fritzing sketch pir1.1 (saved by Fritzing 0.9.3b)
circuit board: 8.46667cm x 5.64444cm
breadboards: 1

parts:
  Componente1 = Arduino Nano (Rev3.0) (ICSP)
  LCM1602_IIC1 = LCM1602 IIC [part_number="LCM1602 IIC" chip_label="LCM1602 IIC" package="DIP (Dual Inline) [THT]"]
  LCD1 = LCD screen
  R1 = Resistor [tolerance=±5% resistance=220 package=THT]
  LED1 = smd LED [color="Red (633nm)" package="0805 [SMD]"]
  LED2 = smd LED [color="Red (633nm)" package="0805 [SMD]"]
  IC1 = DS1302 [package="DIP8 [THT]"]
  S1 = Pushbutton [package="[THT]"]
  S2 = Pushbutton [package="[THT]"]
  S3 = Pushbutton [package="[THT]"]
  R2 = Resistor [tolerance=±5% resistance=1k package=THT]
  R3 = Resistor [tolerance=±5% resistance=1k package=THT]
  R4 = Resistor [tolerance=±5% resistance=1k package=THT]  # not connected
  R5 = Photocell (LDR) [package=THT]
  R6 = Resistor [tolerance=±5% resistance=10k package=THT]

nets:
  GND: Componente1.GND, LCM1602_IIC1.GND, R1.Pin_0, IC1.0V, R6.Pin_0
  N1: Componente1.D2, IC1.CE_-_Chip_Enable
  N2: Componente1.D3, IC1.I/O_-_SPI_Data_In/Out
  N3: Componente1.D4, IC1.SCLK_-_SPI_Clock
  N4: Componente1.D5, LED1.anode, LED2.anode
  5V: Componente1.5V, LCM1602_IIC1.VCC, IC1.+V, R2.Pin_0, R5.pin_1
  N5: Componente1.A7, S1.Pin_1, S1.Pin_2, S2.Pin_1, S2.Pin_2, S3.Pin_1, S3.Pin_2
  N6: Componente1.A5, LCM1602_IIC1.SCL
  N7: Componente1.A4, LCM1602_IIC1.SDA
  N8: Componente1.A0, R5.pin_0, R6.Pin_1
  VSS: LCM1602_IIC1.VSS, LCD1.VSS
  VDD: LCM1602_IIC1.VDD, LCD1.VDD
  N9: LCM1602_IIC1.V0, LCD1.V0
  N10: LCM1602_IIC1.RS, LCD1.RS
  N11: LCM1602_IIC1.RW, LCD1.R/W
  N12: LCM1602_IIC1.E, LCD1.E
  N13: LCM1602_IIC1.D0, LCD1.DB0
  N14: LCM1602_IIC1.D1, LCD1.DB1
  N15: LCM1602_IIC1.D2, LCD1.DB2
  N16: LCM1602_IIC1.D3, LCD1.DB3
  N17: LCM1602_IIC1.D4, LCD1.DB4
  N18: LCM1602_IIC1.D5, LCD1.DB5
  N19: LCM1602_IIC1.D6, LCD1.DB6
  N20: LCM1602_IIC1.D7, LCD1.DB7
  N21: LCM1602_IIC1.A, LCD1.LED+
  N22: LCM1602_IIC1.K, LCD1.LED-
  N23: R1.Pin_1, LED1.cathode, LED2.cathode
  N24: S1.Pin_3, S1.Pin_4, R2.Pin_1, R3.Pin_1
  N25: S2.Pin_3, S2.Pin_4, R3.Pin_0
  N26: S3.Pin_3, S3.Pin_4

notes:
  vcc

custom parts:
  LCM1602 IIC: I2C-Module to use a 1602 or 2004 LCD on with the wire.h libory Serial LCD Modul
